# Fritzing sketch hardware architecture (saved by Fritzing 0.9.3b)

parts:
  Part1 = Arduino Nano (Rev3.0)
  S3 = Round Pushbutton
  M1 = DC Motor
  MD03A1 = Dual VNH2SP30 Motor Driver [part_number=MD03A]
  VCC1 = 4 x AAA Battery Mount
  LCD1 = LCD screen
  U1 = SPM0204UD5 [package=spm0204ud5]

nets:
  GND: Part1.GND, MD03A1.GND#138, LCD1.VSS
  N1: Part1.D4, MD03A1.1INa
  N2: Part1.D5, MD03A1.1INb
  N3: Part1.D6, LCD1.DB2
  N4: Part1.D7, LCD1.DB3
  N5: Part1.D8, LCD1.DB4
  N6: Part1.D9, LCD1.DB5
  N7: Part1.D10, LCD1.DB6
  N8: Part1.D11/MOSI, LCD1.DB7
  N9: Part1.D12/MISO, LCD1.LED+
  N10: Part1.VIN, MD03A1.+5V_(IN)
  N11: Part1.A3, U1.OUT
  N12: Part1.A2, U1.GND
  N13: Part1.3V3, LCD1.LED-
  N14: S3.leg1, MD03A1.VIN
  N15: M1.pin_1, MD03A1.OUT_1A
  N16: M1.pin_2, MD03A1.OUT_1B
  N17: MD03A1.GND#151, VCC1.-

notes:
  Drill motor
  Arduino Nano
  High current motor driver
  Rechargeable battery
  LCD display
  level sensor
